# Fritzing sketch pitch_connections (saved by Fritzing 0.9.3b)

parts:
  Part1 = Arduino Uno (Rev3) - ICSP
  Part2 = Tri-Axis Gyro Breakout - L3G4200D
  Grove1 = Grove OLED 128x96
  M1 = Stepper Motor - Bipolar

nets:
  N1: Part1.A4/SDA, Part2.SDA, Grove1.SDA
  N2: Part1.A5/SCL, Part2.SCL, Grove1.SCL
  N3: Part1.D8, M1.A
  N4: Part1.D9_PWM, M1.C
  N5: Part1.D10_PWM/SS, M1.B
  N6: Part1.D11_PWM/MOSI, M1.D
  GND: Part1.GND, Part2.GND
  VCC: Part2.VCC, Grove1.VCC
