# Fritzing sketch yaw_connections (saved by Fritzing 0.9.3b)

parts:
  Part1 = Arduino Uno (Rev3) - ICSP
  M1 = Stepper Motor - Bipolar

nets:
  N1: Part1.D8, M1.A
  N2: Part1.D9_PWM, M1.C
  N3: Part1.D10_PWM/SS, M1.B
  N4: Part1.D11_PWM/MOSI, M1.D
